# Fritzing sketch Hotel_circuit_diagram (saved by Fritzing 0.8.7b)

parts:
  Launchpad1 = TI Launchpad TM4C123GXL
  Keypad4x1 = Keypad Membran 4x4
  U1 = RELAY-SOLIDSTATE [package=relay-s108t02]
  LED1 = LED - 5mm [color="Red (633nm)" package="5 mm [THT]"]

nets:
  N1: Launchpad1.PB5, Keypad4x1.Pin5
  N2: Launchpad1.PB1, Keypad4x1.Pin6
  N3: Launchpad1.PE1, Keypad4x1.Pin4
  N4: Launchpad1.PE2, Keypad4x1.Pin7
  N5: Launchpad1.PE3, Keypad4x1.Pin8
  N6: Launchpad1.PB3, Keypad4x1.Pin2
  N7: Launchpad1.PB2, Keypad4x1.Pin1
  N8: Launchpad1.PE0, Keypad4x1.Pin3
  N9: Launchpad1.VBUS, U1.+
  N10: Launchpad1.3.3V, LED1.anode
  N11: U1.T2, LED1.cathode

custom parts:
  Keypad Membran 4x4: Membrane Keypad 4x4 Matrix
